# Fritzing sketch scheme (saved by Fritzing 0.9.4)

parts:
  U1 = LuaNode32 / ESP32 [part_number=ESP32S-PIN30]
  DCDC1 = XL4015 DC-DC CC CV module (red)
  U2 = L9110 H-bridge module [part_number="L9110 H-bridge"]
  ZS-042_RTC1 = ZS-042 RTC Module
  M1 = DC Motor
  S1 = Round Pushbutton

nets:
  N1: U1.D14, S1.leg1
  GND: U1.GND, DCDC1.pin_3, ZS-042_RTC1.GND, S1.leg0
  N2: U1.Vin, DCDC1.pin_2
  3V3: U1.3V3, ZS-042_RTC1.VCC
  N3: U1.D18, U2.B-IB
  N4: U1.D19, U2.B-IA
  N5: U1.D21, ZS-042_RTC1.SDA
  N6: U1.D22, ZS-042_RTC1.SCL
  N7: DCDC1.pin_6, U2.VCC
  N8: DCDC1.pin_7, U2.GND
  N9: U2.MOTOR_B-A, M1.pin_2
  N10: U2.MOTOR_B-B, M1.pin_1

custom parts:
  LuaNode32 / ESP32: New Image for LuaNode32 DOIT ESP32 DEVKIT V1. Base parts from LuaNode32 / ESP32 ESP32 based LuaNode32 by G.Noorlander DOIT Esp32 DevKit v1 (30 pins long, 11 pins width) by Werner Rothschopf (modified by vanepp Dec 2018)
  XL4015 DC-DC CC CV module (red): XL4015 DC-DC CC/CV module red
